// Logisim project Adder1.circ as structural Verilog: 1 circuit, main circuit main
module main (
  input  CIN,
  input  X,
  input  Y,
  output SUM,
  output COUT
);

  wire and_1_out, and_2_out, xor_1_out;

  and and_1 (and_1_out, X, Y);
  xor xor_1 (xor_1_out, X, Y);
  or or_1 (COUT, and_1_out, and_2_out);
  and and_2 (and_2_out, CIN, xor_1_out);
  xor xor_2 (SUM, CIN, xor_1_out);
endmodule
