// Logisim project Memory.circ as structural Verilog: 1 circuit, main circuit main
module main (
  input  [7:0] in_1,
  input  Power,
  input  in_3,
  input  in_4,
  output [7:0] out_5,
  output out_6
);

  wire and_1_out, and_2_out, and_3_out, and_4_out, nand_1_out, not_1_out, or_1_out, Reset_out, Set_out;

  Button Reset (.out(Reset_out));
  Button Set (.out(Set_out));
  nand nand_1 (nand_1_out, in_3, in_4);
  not not_1 (not_1_out, Reset_out);
  or or_1 (or_1_out, Set_out, and_3_out);
  nand nand_2 (out_6, nand_1_out, nand_1_out);
  and and_1 (and_1_out, Power, not_1_out);
  and and_2 (and_2_out, not_1_out, or_1_out);
  and and_3 (and_3_out, and_2_out, and_1_out);
  and and_4 (and_4_out, Power, and_2_out);
  Counter counter_1 (.D(in_1), .count(and_4_out), .Q(out_5));  // open: load, carry, clk, clr
  LED led_1 (.in(and_4_out));
endmodule
